// Logisim project asac.circ as structural Verilog: 3 circuits, main circuit channel
module main (
);

  wire and_1_out, and_2_out, clock_1_out, comparator_1_eq, comparator_2_eq, demultiplexer_1_out0,
       demultiplexer_1_out1, demultiplexer_1_out2, demultiplexer_1_out4, pull_resistor_2_node;
  wire [2:0] Microcode_data;
  wire [7:3] Microcode_data_2;
  wire [15:0] PC_q, Program_data_2, pull_resistor_1_node;
  wire [31:0] Program_data;

  Clock clock_1 (.out(clock_1_out));
  and and_1 (and_1_out, clock_1_out, 1'b1);
  // Probe on Program_data_2
  Counter #(.max('hffff), .width(16)) PC (
    .load(comparator_1_eq), .clk(and_1_out), .D(Program_data_2), .Q(PC_q));  // open: clr, up, count, carry
  Comparator comparator_1 (.a({Microcode_data_2, Microcode_data}), .b(8'h42), .eq(comparator_1_eq));  // open: gt, lt
  // Probe on pull_resistor_1_node
  Comparator comparator_2 (.a({Microcode_data_2, Microcode_data}), .b(8'hde), .eq(comparator_2_eq));  // open: gt, lt
  Pull_Resistor pull_resistor_1 (.node(pull_resistor_1_node));
  ROM #(.addrWidth(16), .dataWidth(32)) Program (
    .addr(PC_q), .data({Program_data[31:24], Program_data_2, Program_data[7:0]}));
  Pull_Resistor pull_resistor_2 (.node(pull_resistor_2_node));
  down_counter down_counter_1 (
    .n(Program_data_2), .E(comparator_2_eq), .Clk(clock_1_out), .Val(pull_resistor_1_node),
    .out_5(pull_resistor_2_node));
  // Probe on Program_data[7:0]
  ROM Microcode (.addr(Program_data[7:0]), .data({Microcode_data_2, Microcode_data}));
  // Probe on {Microcode_data_2, Microcode_data}
  LED led_1 (.in(demultiplexer_1_out0));
  LED led_2 (.in(demultiplexer_1_out1));
  LED led_3 (.in(demultiplexer_1_out2));
  LED led_4 (.in(demultiplexer_1_out4));
  Demultiplexer #(.select(3)) demultiplexer_1 (
    .out0(demultiplexer_1_out0), .out1(demultiplexer_1_out1), .out2(demultiplexer_1_out2),
    .out4(demultiplexer_1_out4), .in(and_2_out), .sel(Microcode_data));  // open: out3, out5, out6, out7
  and and_2 (and_2_out, Microcode_data_2[5], Microcode_data_2[3]);
  channel channel_1 (
    .f(Program_data_2), .v(Program_data[31:24]), .Set(Microcode_data_2[4]), .E(demultiplexer_1_out4),
    .Clk(clock_1_out));
  channel channel_2 (
    .f(Program_data_2), .v(Program_data[31:24]), .Set(Microcode_data_2[4]), .E(demultiplexer_1_out2),
    .Clk(clock_1_out));
  // Probe on Program_data_2
  // Probe on Program_data[31:24]
  channel channel_3 (
    .f(Program_data_2), .v(Program_data[31:24]), .Set(Microcode_data_2[4]), .E(demultiplexer_1_out1),
    .Clk(clock_1_out));
  channel channel_4 (
    .f(Program_data_2), .v(Program_data[31:24]), .Set(Microcode_data_2[4]), .E(demultiplexer_1_out0),
    .Clk(clock_1_out));

  // Notes on the sheet:
  //   contents of Program (hex, n*v repeats v):
  //   7f03e804 7f01f405 7f006406 7f000007 9
  //   contents of Microcode (hex, n*v repeats v):
  //   28 29 2a 2c 38 39 3a 3c de 42
endmodule

module channel (
  input  [15:0] f,
  input  [7:0] v,
  input  Set,
  input  E,
  input  Clk
);

  wire register_1_q;
  wire [7:0] Vol_q;
  wire [15:0] Freq_q;

  Register #(.width(16)) Freq (.D(f), .en(E), .clk(Clk), .Q(Freq_q));  // open: clr
  Register Vol (.D(v), .en(E), .clk(Clk), .Q(Vol_q));  // open: clr
  Register #(.width(1)) register_1 (.D(Set), .en(E), .clk(Clk), .Q(register_1_q));  // open: clr
  // Buzzer #(.vol_width(8)) buzzer_1: pin names not known; wires that end beside it: Freq_q[13:0], register_1_q, Vol_q
endmodule

module down_counter (
  input  [15:0] n,
  input  E,
  input  Clk,
  input  [15:0] Val,
  output out_5
);

  wire [15:0] register_1_q;

  Counter #(.max('hffff), .width(16)) counter_1 (.clr(E), .clk(Clk), .D(n), .Q(Val));  // open: load, up, count, carry
  Register #(.width(16)) register_1 (.D(n), .en(E), .clk(Clk), .Q(register_1_q));  // open: clr
  Comparator #(.width(16)) comparator_1 (.a(Val), .b(register_1_q), .eq(out_5));  // open: gt, lt
endmodule
